# Fritzing sketch schematic (saved by Fritzing 0.9.4)

parts:
  Composant1 = Arduino Due (Rev2b)
  M2 = ESC
  920KV_Motor2 = DJI 920 KV Motor
  Power_plug2 = Power plug  # not connected
  920KV_Motor3 = DJI 920 KV Motor
  M3 = ESC
  M4 = ESC
  920KV_Motor4 = DJI 920 KV Motor
  M5 = ESC
  920KV_Motor5 = DJI 920 KV Motor
  ANT1 = Antenna
  Power_plug3 = Power plug
  M6 = gy9250

nets:
  N1: Composant1.IOREF, M6.pin1
  N2: Composant1.GND, M6.pin2
  N3: Composant1.D8_PWM, M4.DATA
  N4: Composant1.D9_PWM, M5.DATA
  N5: Composant1.D4_PWM/SS1, M6.pin9
  N6: Composant1.D5_PWM, ANT1.C3
  N7: Composant1.D6_PWM, M2.DATA
  N8: Composant1.D7_PWM, M3.DATA
  N9: M2.U, 920KV_Motor2.u
  N10: M2.V, 920KV_Motor2.v
  N11: M2.W, 920KV_Motor2.w
  N12: 920KV_Motor3.w, M3.W
  N13: 920KV_Motor3.v, M3.V
  N14: 920KV_Motor3.u, M3.U
  N15: M4.U, 920KV_Motor4.u
  N16: M4.V, 920KV_Motor4.v
  N17: M4.W, 920KV_Motor4.w
  N18: M5.U, 920KV_Motor5.u
  N19: M5.V, 920KV_Motor5.v
  N20: M5.W, 920KV_Motor5.w
  GND: ANT1.GND, Power_plug3.GND
  VCC: ANT1.VCC, Power_plug3.VCC

notes:
  11.1V 3S Battery
  Motor A
  Motor B
  Motor C
  Motor D
  5V
  Connect VIN when Arduino is not powered by microUSB

custom parts:
  DJI 920 KV Motor: DJI Brushless Outrunner 2212/920K Motor F330-550
  Antenna: Random Wire Antenna
  gy9250: MPU-9250 module (three-axis gyroscope + three-axis acceleration + three-axis magnetic field). The generic model from ebay et. al. rather than the Sparkfun version.
